// Logisim project Exp-1.circ as structural Verilog: 1 circuit, main circuit main
module main (
  input  in_1,
  input  in_2,
  input  in_3,
  input  in_4,
  input  in_5,
  input  in_6,
  input  in_7,
  input  in_8,
  input  in_9,
  input  in_10,
  input  in_11,
  output out_12,
  output out_13,
  output out_14,
  output out_15,
  output out_16,
  output out_17
);

  not not_1 (out_12, in_1);
  and and_1 (out_13, in_2, in_3);
  or or_1 (out_14, in_4, in_5);
  nand nand_1 (out_15, in_6, in_7);
  nor nor_1 (out_16, in_8, in_9);
  xor xor_1 (out_17, in_10, in_11);

  // Notes on the sheet:
  //   Exp-1  
  //   * NOT GATE -- Using IC 7404(Hex Inverter)
  //   * OR GATE - Using IC 7432(Quad 2I/P OR Gate)
  //   * NAND GATE - Using IC 7400(Quad 2I/P NAND Gate)
  //   * XOR GATE - Using IC 7486(Quad 2I/P XOR Gate)
  //   * AND GATE -- Using IC 7408(Quad 2I/P AND GAte)
  //   * NOR GATE - Using IC 7402(Quad 2I/P NOR Gate - pIN Config is different that usual)
  //   Study & Verification of Truth tables of Different Basic Logic gates(AND,OR,NOT,NAND,NOR,XOR) 
  //   0
  //   0
  //   1
  //   1
  //   0
  //   0
  //   1
  //   1
  //   0
  //   0
  //   1
  //   1
  //   0
  //   0
  //   1
  //   1
  //   0
  //   0
  //   1
  //   1
  //   Truth Table
  //   X(Input)   |   Y(Ouput)
  //   1
  //   0
  //   Truth Table
  //   X1 (Input)  |   X2(Input)  |   Y(Ouput)
  //   0
  //   1
  //   0
  //   1
  //   Truth Table
  //   X1 (Input)  |   X2(Input)  |   Y(Ouput)
  //   0
  //   1
  //   0
  //   1
  //   Truth Table
  //   X1 (Input)  |   X2(Input)  |   Y(Ouput)
  //   0
  //   1
  //   0
  //   1
  //   Truth Table
  //   X1 (Input)  |   X2(Input)  |   Y(Ouput)
  //   0
  //   1
  //   0
  //   1
  //   Truth Table
  //   X1 (Input)  |   X2(Input)  |   Y(Ouput)
  //   0
  //   1
  //   0
  //   1
  //   0
  //   1
  //   0
  //   0
  //   0
  //   1
  //   0
  //   1
  //   1
  //   1
  //   1
  //   1
  //   1
  //   0
  //   1
  //   0
  //   0
  //   0
  //   0
  //   1
  //   1
  //   0
endmodule
